// Logisim project P3.circ as structural Verilog: 8 circuits, main circuit main
module main (
  input  RESET,
  output [31:0] out_2,
  output [31:0] out_3,
  output out_4,
  output [4:0] out_5,
  output [31:0] out_6,
  output out_7,
  output [31:0] out_8,
  output [31:0] out_9
);

  wire bcheck_1_check, clk_out, controller_1_alusrc, controller_1_memtoreg, controller_1_npc_sel,
       controller_1_regdst;
  wire [1:0] controller_1_out_10, controller_1_out_11;
  wire [5:0] controller_1_bop;
  wire [11:0] MemAddr;
  wire [31:0] alu_1_out_4, ext_1_out_3, grf_1_out_8, multiplexer_2_out, ram_1_data;

  Clock clk (.out(clk_out));
  IFU ifu_1 (
    .if_branch(bcheck_1_check), .out_6(out_2), .RESET(RESET), .CLK(clk_out), .offset(ext_1_out_3),
    .out_5(out_3));
  // Probe on out_2[31:26]
  // Probe on out_2
  // Probe on out_2[5:0]
  // Probe on out_2[25:21]
  Controller controller_1 (
    .OpCode(out_2[31:26]), .Funct(out_2[5:0]), .RegDst(controller_1_regdst), .ALUSrc(controller_1_alusrc),
    .MemtoReg(controller_1_memtoreg), .RegWrite(out_4), .MemWrite(out_7), .nPC_sel(controller_1_npc_sel),
    .out_10(controller_1_out_10), .out_11(controller_1_out_11), .bOp(controller_1_bop));
  // Probe on out_2[20:16]
  // Probe on out_2[15:11]
  // Probe on out_2[10:6]
  // Probe on out_2[15:0]
  // Probe on {out_2[20:11], out_2[15:0]}
  bCheck bcheck_1 (
    .Grs(grf_1_out_8), .Grt(out_9), .bOp(controller_1_bop), .branch(controller_1_npc_sel),
    .check(bcheck_1_check));
  Multiplexer #(.width(5), .enable("false")) multiplexer_1 (
    .in0(out_2[20:16]), .in1(out_2[15:11]), .out(out_5), .sel(controller_1_regdst));
  // Probe on out_6
  GRF grf_1 (
    .in_1(out_2[25:21]), .in_5(out_2[20:16]), .in_6(out_5), .in_7(out_6), .out_8(grf_1_out_8), .out_9(out_9),
    .in_2(clk_out), .in_3(RESET), .in_4(out_4));
  EXT ext_1 (.in_2(out_2[15:0]), .out_3(ext_1_out_3), .in_1(controller_1_out_10));
  Multiplexer #(.width(32), .enable("false")) multiplexer_2 (
    .in0(out_9), .in1(ext_1_out_3), .out(multiplexer_2_out), .sel(controller_1_alusrc));
  Multiplexer #(.width(32), .enable("false")) multiplexer_3 (
    .in0(alu_1_out_4), .in1(ram_1_data), .out(out_6), .sel(controller_1_memtoreg));
  // Probe on alu_1_out_4
  ALU alu_1 (.A(grf_1_out_8), .B(multiplexer_2_out), .F(controller_1_out_11), .out_4(alu_1_out_4));
  Bit_Extender #(.in_width(32), .out_width(12)) bit_extender_1 (.in(alu_1_out_4), .out(MemAddr));
  RAM #(.addrWidth(12), .dataWidth(32), .bus("separate")) ram_1 (
    .addr(MemAddr), .din(out_9), .data(ram_1_data), .str(out_7), .clk(clk_out));  // open: sel, ld, clr
  assign out_8 = {{20{1'b0}}, MemAddr};  // Bit_Extender bit_extender_2

  // Other names for the same wires on the sheet: Instr[31:0] = out_2; MemData[31:0] = out_9; MemWrite = out_7;
  //   pc[31:0] = out_3; RegAddr[4:0] = out_5; RegData[31:0] = out_6; RegWrite = out_4
endmodule

module IFU (
  input  [31:0] offset,
  input  if_branch,
  input  CLK,
  input  RESET,
  output [31:0] out_5,
  output [31:0] out_6
);

  wire counter_1_q;
  wire [11:0] bit_extender_1_out;
  wire [31:0] adder_1_out, adder_2_out, multiplexer_2_out, PC_q, shifter_1_out, shifter_2_out,
       subtractor_1_out;

  Register #(.width(32)) PC (.D(adder_2_out), .Q(PC_q), .clk(CLK), .clr(RESET));  // open: en
  Multiplexer #(.width(32), .enable("false")) multiplexer_1 (
    .in0(32'h3000), .in1(PC_q), .out(out_5), .sel(counter_1_q));
  Counter #(.width(1), .max('h1), .ongoal("stay")) counter_1 (
    .Q(counter_1_q), .clk(CLK), .clr(RESET));  // open: load, D, count, carry
  Shifter #(.width(32)) shifter_1 (.in(offset), .\dist (5'b00010), .out(shifter_1_out));
  Adder #(.width(32)) adder_1 (.a(32'h4), .b(out_5), .out(adder_1_out));  // open: cin, cout
  Multiplexer #(.width(32), .disabled(0), .enable("false")) multiplexer_2 (
    .in0({32{1'b0}}), .in1(shifter_1_out), .out(multiplexer_2_out), .sel(if_branch));
  Subtractor #(.width(32)) subtractor_1 (.a(out_5), .b(32'h3000), .out(subtractor_1_out));  // open: bin, bout
  Shifter #(.width(32), .shift("lr")) shifter_2 (.in(subtractor_1_out), .\dist (5'b00010), .out(shifter_2_out));
  Bit_Extender #(.in_width(32), .out_width(12)) bit_extender_1 (.in(shifter_2_out), .out(bit_extender_1_out));
  Adder #(.width(32)) adder_2 (.a(adder_1_out), .b(multiplexer_2_out), .out(adder_2_out));  // open: cin, cout
  ROM #(.addrWidth(12), .dataWidth(32)) rom_1 (.addr(bit_extender_1_out), .data(out_6));  // open: sel

  // Notes on the sheet:
  //   contents of rom_1 (hex, n*v repeats v):
  //   36310001 00000000 02318820 02318820 02318820 02318820 02318820 02318820 02318820 02318820
endmodule

module GRF (
  input  [4:0] in_1,
  input  in_2,
  input  in_3,
  input  in_4,
  input  [4:0] in_5,
  input  [4:0] in_6,
  input  [31:0] in_7,
  output [31:0] out_8,
  output [31:0] out_9
);

  wire _0_we, _1_we, _2_we, _3_we, _4_we, _5_we, _6_we, _7_we, _8_we, _9_we, _10_we, _11_we, _12_we, _13_we,
       _14_we, _15_we, _16_we, _17_we, _18_we, _19_we, _20_we, _21_we, _22_we, _23_we, _24_we, _25_we,
       _26_we, _27_we, _28_we, _29_we, _30_we, _31_we;
  wire [31:0] _0, _0_out, _1, _1_out, _2, _2_out, _3, _3_out, _4, _4_out, _5, _5_out, _6, _6_out, _7, _7_out,
       _8, _8_out, _9, _9_out, _10, _10_out, _11, _11_out, _12, _12_out, _13, _13_out, _14, _14_out, _15,
       _15_out, _16, _16_out, _17, _17_out, _18, _18_out, _19, _19_out, _20, _20_out, _21, _21_out, _22,
       _22_out, _23, _23_out, _24, _24_out, _25, _25_out, _26, _26_out, _27, _27_out, _28, _28_out, _29,
       _29_out, _30, _30_out, _31, _31_out;

  Demultiplexer #(.select(5), .width(32), .enable("false")) demultiplexer_1 (
    .out0(_0), .out1(_1), .out2(_2), .out3(_3), .out4(_4), .out5(_5), .out6(_6), .out7(_7), .out8(_8),
    .out9(_9), .out10(_10), .out11(_11), .out12(_12), .out13(_13), .out14(_14), .out15(_15), .out16(_16),
    .out17(_17), .out18(_18), .out19(_19), .out20(_20), .out21(_21), .out22(_22), .out23(_23), .out24(_24),
    .out25(_25), .out26(_26), .out27(_27), .out28(_28), .out29(_29), .out30(_30), .out31(_31), .in(in_7),
    .sel(in_6));
  Multiplexer #(.select(5), .width(32), .enable("false")) multiplexer_1 (
    .in0(_0_out), .in1(_1_out), .in2(_2_out), .in3(_3_out), .in4(_4_out), .in5(_5_out), .in6(_6_out),
    .in7(_7_out), .in8(_8_out), .in9(_9_out), .in10(_10_out), .in11(_11_out), .in12(_12_out), .in13(_13_out),
    .in14(_14_out), .in15(_15_out), .in16(_16_out), .in17(_17_out), .in18(_18_out), .in19(_19_out),
    .in20(_20_out), .in21(_21_out), .in22(_22_out), .in23(_23_out), .in24(_24_out), .in25(_25_out),
    .in26(_26_out), .in27(_27_out), .in28(_28_out), .in29(_29_out), .in30(_30_out), .in31(_31_out),
    .out(out_8), .sel(in_1));
  Demultiplexer #(.select(5), .enable("false")) demultiplexer_2 (
    .out0(_0_we), .out1(_1_we), .out2(_2_we), .out3(_3_we), .out4(_4_we), .out5(_5_we), .out6(_6_we),
    .out7(_7_we), .out8(_8_we), .out9(_9_we), .out10(_10_we), .out11(_11_we), .out12(_12_we), .out13(_13_we),
    .out14(_14_we), .out15(_15_we), .out16(_16_we), .out17(_17_we), .out18(_18_we), .out19(_19_we),
    .out20(_20_we), .out21(_21_we), .out22(_22_we), .out23(_23_we), .out24(_24_we), .out25(_25_we),
    .out26(_26_we), .out27(_27_we), .out28(_28_we), .out29(_29_we), .out30(_30_we), .out31(_31_we),
    .in(in_4), .sel(in_6));
  Register #(.width(32)) u__0 (.D({32{1'b0}}), .en(_0_we), .Q(_0_out), .clk(in_2), .clr(in_3));
  Register #(.width(32)) u__8 (.D(_8), .en(_8_we), .Q(_8_out), .clk(in_2), .clr(in_3));
  Register #(.width(32)) u__16 (.D(_16), .en(_16_we), .Q(_16_out), .clk(in_2), .clr(in_3));
  Register #(.width(32)) u__24 (.D(_24), .en(_24_we), .Q(_24_out), .clk(in_2), .clr(in_3));
  Register #(.width(32)) u__1 (.D(_1), .en(_1_we), .Q(_1_out), .clk(in_2), .clr(in_3));
  Register #(.width(32)) u__9 (.D(_9), .en(_9_we), .Q(_9_out), .clk(in_2), .clr(in_3));
  Register #(.width(32)) u__17 (.D(_17), .en(_17_we), .Q(_17_out), .clk(in_2), .clr(in_3));
  Register #(.width(32)) u__25 (.D(_25), .en(_25_we), .Q(_25_out), .clk(in_2), .clr(in_3));
  Register #(.width(32)) u__2 (.D(_2), .en(_2_we), .Q(_2_out), .clk(in_2), .clr(in_3));
  Register #(.width(32)) u__10 (.D(_10), .en(_10_we), .Q(_10_out), .clk(in_2), .clr(in_3));
  Register #(.width(32)) u__18 (.D(_18), .en(_18_we), .Q(_18_out), .clk(in_2), .clr(in_3));
  Register #(.width(32)) u__26 (.D(_26), .en(_26_we), .Q(_26_out), .clk(in_2), .clr(in_3));
  Multiplexer #(.select(5), .width(32), .enable("false")) multiplexer_2 (
    .in0(_0_out), .in1(_1_out), .in2(_2_out), .in3(_3_out), .in4(_4_out), .in5(_5_out), .in6(_6_out),
    .in7(_7_out), .in8(_8_out), .in9(_9_out), .in10(_10_out), .in11(_11_out), .in12(_12_out), .in13(_13_out),
    .in14(_14_out), .in15(_15_out), .in16(_16_out), .in17(_17_out), .in18(_18_out), .in19(_19_out),
    .in20(_20_out), .in21(_21_out), .in22(_22_out), .in23(_23_out), .in24(_24_out), .in25(_25_out),
    .in26(_26_out), .in27(_27_out), .in28(_28_out), .in29(_29_out), .in30(_30_out), .in31(_31_out),
    .out(out_9), .sel(in_5));
  Register #(.width(32)) u__3 (.D(_3), .en(_3_we), .Q(_3_out), .clk(in_2), .clr(in_3));
  Register #(.width(32)) u__11 (.D(_11), .en(_11_we), .Q(_11_out), .clk(in_2), .clr(in_3));
  Register #(.width(32)) u__19 (.D(_19), .en(_19_we), .Q(_19_out), .clk(in_2), .clr(in_3));
  Register #(.width(32)) u__27 (.D(_27), .en(_27_we), .Q(_27_out), .clk(in_2), .clr(in_3));
  Register #(.width(32)) u__4 (.D(_4), .en(_4_we), .Q(_4_out), .clk(in_2), .clr(in_3));
  Register #(.width(32)) u__12 (.D(_12), .en(_12_we), .Q(_12_out), .clk(in_2), .clr(in_3));
  Register #(.width(32)) u__20 (.D(_20), .en(_20_we), .Q(_20_out), .clk(in_2), .clr(in_3));
  Register #(.width(32)) u__28 (.D(_28), .en(_28_we), .Q(_28_out), .clk(in_2), .clr(in_3));
  Register #(.width(32)) u__5 (.D(_5), .en(_5_we), .Q(_5_out), .clk(in_2), .clr(in_3));
  Register #(.width(32)) u__13 (.D(_13), .en(_13_we), .Q(_13_out), .clk(in_2), .clr(in_3));
  Register #(.width(32)) u__21 (.D(_21), .en(_21_we), .Q(_21_out), .clk(in_2), .clr(in_3));
  Register #(.width(32)) u__29 (.D(_29), .en(_29_we), .Q(_29_out), .clk(in_2), .clr(in_3));
  Register #(.width(32)) u__6 (.D(_6), .en(_6_we), .Q(_6_out), .clk(in_2), .clr(in_3));
  Register #(.width(32)) u__30 (.D(_30), .en(_30_we), .Q(_30_out), .clk(in_2), .clr(in_3));
  Register #(.width(32)) u__14 (.D(_14), .en(_14_we), .Q(_14_out), .clk(in_2), .clr(in_3));
  Register #(.width(32)) u__22 (.D(_22), .en(_22_we), .Q(_22_out), .clk(in_2), .clr(in_3));
  Register #(.width(32)) u__7 (.D(_7), .en(_7_we), .Q(_7_out), .clk(in_2), .clr(in_3));
  Register #(.width(32)) u__15 (.D(_15), .en(_15_we), .Q(_15_out), .clk(in_2), .clr(in_3));
  Register #(.width(32)) u__23 (.D(_23), .en(_23_we), .Q(_23_out), .clk(in_2), .clr(in_3));
  Register #(.width(32)) u__31 (.D(_31), .en(_31_we), .Q(_31_out), .clk(in_2), .clr(in_3));

  // Other names for the same wires on the sheet: A1[4:0] = in_1; A2[4:0] = in_5; A3[4:0] = in_6; clk = in_2;
  //   RD1[31:0] = out_8; RD2[31:0] = out_9; reset = in_3; WD[31:0] = in_7; WE = in_4
endmodule

module ALU (
  input  [1:0] F,
  input  [31:0] A,
  input  [31:0] B,
  output [31:0] out_4
);

  wire [31:0] adder_1_out, or_1_out, shifter_1_out, subtractor_1_out;

  Adder #(.width(32)) adder_1 (.a(A), .b(B), .out(adder_1_out));  // open: cin, cout
  Subtractor #(.width(32)) subtractor_1 (.a(A), .b(B), .out(subtractor_1_out));  // open: bin, bout
  assign or_1_out = A | B;  // OR_Gate or_1, 32 bits wide
  Shifter #(.width(32)) shifter_1 (.in(B), .\dist (5'b10000), .out(shifter_1_out));
  Multiplexer #(.select(2), .width(32), .enable("false")) multiplexer_1 (
    .in0(adder_1_out), .in1(subtractor_1_out), .in2(or_1_out), .in3(shifter_1_out), .out(out_4), .sel(F));
endmodule

module Controller (
  input  [5:0] OpCode,
  input  [5:0] Funct,
  output [5:0] bOp,
  output RegDst,
  output ALUSrc,
  output MemtoReg,
  output RegWrite,
  output MemWrite,
  output nPC_sel,
  output [1:0] out_10,
  output [1:0] out_11
);

  wire add_out, and_1_out, and_2_out, and_5_out, and_6_out, and_7_out, and_8_out, and_10_out, and_11_out,
       and_12_out, and_13_out, and_14_out, and_15_out, and_16_out, lui_out, not_1_out, not_2_out, not_3_out,
       not_4_out, not_5_out, not_6_out, not_7_out, not_8_out, not_9_out, not_10_out, not_11_out, not_12_out,
       not_13_out, not_14_out, not_15_out, not_16_out, not_17_out, not_18_out, not_19_out, not_20_out,
       not_21_out, not_22_out, not_23_out, not_24_out, not_25_out, not_26_out, not_27_out, not_28_out,
       not_29_out, not_30_out, not_31_out, not_32_out, not_33_out, not_34_out, not_35_out, not_36_out,
       not_37_out, not_38_out, not_39_out, not_40_out, not_41_out, not_42_out, not_43_out, not_44_out,
       not_45_out, not_46_out, not_47_out, not_48_out, not_49_out, not_50_out, not_51_out, not_52_out,
       not_53_out, not_54_out, not_55_out, not_56_out, not_57_out, not_58_out, not_59_out, not_60_out,
       not_61_out, ori_out, R_type_out, sub_out;

  and add (add_out, Funct[5], ~Funct[4], ~Funct[3], ~Funct[2], ~Funct[1], ~Funct[0]);  // AND_Gate
  and and_1 (and_1_out, add_out, R_type_out);
  and sub (sub_out, Funct[5], ~Funct[4], ~Funct[3], ~Funct[2], Funct[1], ~Funct[0]);  // AND_Gate
  and and_2 (and_2_out, sub_out, R_type_out);
  and R_type (R_type_out, ~OpCode[5], ~OpCode[4], ~OpCode[3], ~OpCode[2], ~OpCode[1], ~OpCode[0]);  // AND_Gate
  and ori (ori_out, ~OpCode[5], ~OpCode[4], OpCode[3], OpCode[2], ~OpCode[1], OpCode[0]);  // AND_Gate
  and lw (MemtoReg, OpCode[5], ~OpCode[4], ~OpCode[3], ~OpCode[2], OpCode[1], OpCode[0]);  // AND_Gate
  and sw (MemWrite, OpCode[5], ~OpCode[4], OpCode[3], ~OpCode[2], OpCode[1], OpCode[0]);  // AND_Gate
  and beq (bOp[5], ~OpCode[5], ~OpCode[4], ~OpCode[3], OpCode[2], ~OpCode[1], ~OpCode[0]);  // AND_Gate
  and lui (lui_out, ~OpCode[5], ~OpCode[4], OpCode[3], OpCode[2], OpCode[1], OpCode[0]);  // AND_Gate
  and bgez (bOp[4], ~OpCode[5], ~OpCode[4], ~OpCode[3], ~OpCode[2], ~OpCode[1], OpCode[0]);  // AND_Gate
  and bgtz (bOp[3], ~OpCode[5], ~OpCode[4], ~OpCode[3], OpCode[2], OpCode[1], OpCode[0]);  // AND_Gate
  and blez (bOp[2], ~OpCode[5], ~OpCode[4], ~OpCode[3], OpCode[2], OpCode[1], ~OpCode[0]);  // AND_Gate
  not not_1 (not_1_out, ori_out);
  not not_2 (not_2_out, MemtoReg);
  not not_3 (not_3_out, MemWrite);
  not not_4 (not_4_out, bOp[5]);
  not not_5 (not_5_out, lui_out);
  not not_6 (not_6_out, and_1_out);
  not not_7 (not_7_out, and_2_out);
  not not_8 (not_8_out, and_1_out);
  not not_9 (not_9_out, and_2_out);
  not not_10 (not_10_out, ori_out);
  not not_11 (not_11_out, MemtoReg);
  not not_12 (not_12_out, MemWrite);
  not not_13 (not_13_out, bOp[5]);
  not not_14 (not_14_out, and_1_out);
  not not_15 (not_15_out, and_2_out);
  not not_16 (not_16_out, ori_out);
  not not_17 (not_17_out, MemWrite);
  not not_18 (not_18_out, bOp[5]);
  not not_19 (not_19_out, lui_out);
  not not_20 (not_20_out, and_1_out);
  not not_21 (not_21_out, and_2_out);
  not not_22 (not_22_out, MemtoReg);
  not not_23 (not_23_out, MemWrite);
  not not_24 (not_24_out, bOp[5]);
  not not_25 (not_25_out, lui_out);
  not not_26 (not_26_out, ori_out);
  not not_27 (not_27_out, MemtoReg);
  not not_28 (not_28_out, MemWrite);
  not not_29 (not_29_out, bOp[5]);
  not not_30 (not_30_out, lui_out);
  not not_31 (not_31_out, and_1_out);
  not not_32 (not_32_out, and_2_out);
  not not_33 (not_33_out, ori_out);
  not not_34 (not_34_out, and_1_out);
  not not_35 (not_35_out, and_2_out);
  not not_36 (not_36_out, MemtoReg);
  not not_37 (not_37_out, MemWrite);
  not not_38 (not_38_out, bOp[5]);
  not not_39 (not_39_out, lui_out);
  not not_40 (not_40_out, and_1_out);
  not not_41 (not_41_out, and_2_out);
  not not_42 (not_42_out, lui_out);
  not not_43 (not_43_out, and_1_out);
  not not_44 (not_44_out, and_2_out);
  not not_45 (not_45_out, lui_out);
  not not_46 (not_46_out, and_1_out);
  not not_47 (not_47_out, and_2_out);
  not not_48 (not_48_out, lui_out);
  not not_49 (not_49_out, and_1_out);
  not not_50 (not_50_out, and_2_out);
  not not_51 (not_51_out, lui_out);
  not not_52 (not_52_out, and_1_out);
  not not_53 (not_53_out, and_2_out);
  not not_54 (not_54_out, MemtoReg);
  not not_55 (not_55_out, MemWrite);
  not not_56 (not_56_out, bOp[5]);
  not not_57 (not_57_out, and_1_out);
  not not_58 (not_58_out, ori_out);
  not not_59 (not_59_out, MemtoReg);
  not not_60 (not_60_out, MemWrite);
  not not_61 (not_61_out, bOp[5]);
  and bltz (bOp[1], ~OpCode[5], ~OpCode[4], ~OpCode[3], ~OpCode[2], ~OpCode[1], OpCode[0]);  // AND_Gate
  and and_3 (RegDst, not_1_out, not_2_out, not_3_out, not_4_out, not_5_out);
  and and_4 (ALUSrc, not_6_out, not_7_out);
  and and_5 (and_5_out, not_8_out, not_9_out, not_10_out, not_11_out, not_12_out, not_13_out);
  and and_6 (and_6_out, not_14_out, not_15_out, not_16_out, not_17_out, not_18_out, not_19_out);
  and and_7 (and_7_out, not_20_out, not_21_out, not_22_out, not_23_out, not_24_out, not_25_out);
  and and_8 (and_8_out, not_26_out, not_27_out, not_28_out, not_29_out, not_30_out);
  and and_9 (out_10[1], not_31_out, not_32_out, not_33_out);
  and and_10 (and_10_out, not_34_out, not_35_out, not_36_out, not_37_out, not_38_out, not_39_out);
  and and_11 (and_11_out, not_40_out, not_41_out, MemWrite, bOp[5], not_42_out);
  and and_12 (and_12_out, not_43_out, not_44_out, MemtoReg, bOp[5], not_45_out);
  and and_13 (and_13_out, not_46_out, not_47_out, MemtoReg, MemWrite, not_48_out);
  and and_14 (and_14_out, not_49_out, not_50_out, ori_out, not_51_out);
  and and_15 (and_15_out, not_52_out, not_53_out, not_54_out, not_55_out, not_56_out, lui_out);
  and and_16 (and_16_out, not_57_out, not_58_out, not_59_out, not_60_out, not_61_out, lui_out);
  or or_1 (RegWrite, and_5_out, and_6_out, and_7_out, and_8_out);
  or or_2 (out_10[0], and_10_out, and_11_out, and_12_out, and_13_out, and_14_out);
  or or_3 (out_11[1], and_15_out, ori_out);
  or or_4 (out_11[0], and_16_out, and_2_out);
  and bne (bOp[0], ~OpCode[5], ~OpCode[4], ~OpCode[3], OpCode[2], ~OpCode[1], OpCode[0]);  // AND_Gate

  assign nPC_sel = bOp[5];
endmodule

module tureTable (
  input  add,
  input  sub,
  input  ori,
  input  lw,
  input  sw,
  input  beq,
  input  lui,
  output RegDst,
  output ALUSrc,
  output MemtoReg,
  output RegWrite,
  output MemWrite,
  output nPC_sel,
  output ExtOp_1,
  output ExtOp_0,
  output ALUctr_1,
  output ALUctr_0
);

  wire and_3_out, and_4_out, and_5_out, and_6_out, and_8_out, and_9_out, and_10_out, and_11_out, and_12_out,
       and_13_out, and_14_out, not_1_out, not_2_out, not_3_out, not_4_out, not_5_out, not_6_out, not_7_out,
       not_8_out, not_9_out, not_10_out, not_11_out, not_12_out, not_13_out, not_14_out, not_15_out,
       not_16_out, not_17_out, not_18_out, not_19_out, not_20_out, not_21_out, not_22_out, not_23_out,
       not_24_out, not_25_out, not_26_out, not_27_out, not_28_out, not_29_out, not_30_out, not_31_out,
       not_32_out, not_33_out, not_34_out, not_35_out, not_36_out, not_37_out, not_38_out, not_39_out,
       not_40_out, not_41_out, not_42_out, not_43_out, not_44_out, not_45_out, not_46_out, not_47_out,
       not_48_out, not_49_out, not_50_out, not_51_out, not_52_out, not_53_out, not_54_out, not_55_out,
       not_56_out, not_57_out, not_58_out, not_59_out, not_60_out, not_61_out;

  not not_1 (not_1_out, ori);
  not not_2 (not_2_out, lw);
  not not_3 (not_3_out, sw);
  not not_4 (not_4_out, beq);
  not not_5 (not_5_out, lui);
  not not_6 (not_6_out, add);
  not not_7 (not_7_out, sub);
  not not_8 (not_8_out, add);
  not not_9 (not_9_out, sub);
  not not_10 (not_10_out, ori);
  not not_11 (not_11_out, lw);
  not not_12 (not_12_out, sw);
  not not_13 (not_13_out, beq);
  not not_14 (not_14_out, add);
  not not_15 (not_15_out, sub);
  not not_16 (not_16_out, ori);
  not not_17 (not_17_out, sw);
  not not_18 (not_18_out, beq);
  not not_19 (not_19_out, lui);
  not not_20 (not_20_out, add);
  not not_21 (not_21_out, sub);
  not not_22 (not_22_out, lw);
  not not_23 (not_23_out, sw);
  not not_24 (not_24_out, beq);
  not not_25 (not_25_out, lui);
  not not_26 (not_26_out, ori);
  not not_27 (not_27_out, lw);
  not not_28 (not_28_out, sw);
  not not_29 (not_29_out, beq);
  not not_30 (not_30_out, lui);
  not not_31 (not_31_out, add);
  not not_32 (not_32_out, sub);
  not not_33 (not_33_out, ori);
  not not_34 (not_34_out, add);
  not not_35 (not_35_out, sub);
  not not_36 (not_36_out, lw);
  not not_37 (not_37_out, sw);
  not not_38 (not_38_out, beq);
  not not_39 (not_39_out, lui);
  not not_40 (not_40_out, add);
  not not_41 (not_41_out, sub);
  not not_42 (not_42_out, lui);
  not not_43 (not_43_out, add);
  not not_44 (not_44_out, sub);
  not not_45 (not_45_out, lui);
  not not_46 (not_46_out, add);
  not not_47 (not_47_out, sub);
  not not_48 (not_48_out, lui);
  not not_49 (not_49_out, add);
  not not_50 (not_50_out, sub);
  not not_51 (not_51_out, lui);
  not not_52 (not_52_out, add);
  not not_53 (not_53_out, sub);
  not not_54 (not_54_out, lw);
  not not_55 (not_55_out, sw);
  not not_56 (not_56_out, beq);
  not not_57 (not_57_out, add);
  not not_58 (not_58_out, ori);
  not not_59 (not_59_out, lw);
  not not_60 (not_60_out, sw);
  not not_61 (not_61_out, beq);
  and and_1 (RegDst, not_1_out, not_2_out, not_3_out, not_4_out, not_5_out);
  and and_2 (ALUSrc, not_6_out, not_7_out);
  and and_3 (and_3_out, not_8_out, not_9_out, not_10_out, not_11_out, not_12_out, not_13_out);
  and and_4 (and_4_out, not_14_out, not_15_out, not_16_out, not_17_out, not_18_out, not_19_out);
  and and_5 (and_5_out, not_20_out, not_21_out, not_22_out, not_23_out, not_24_out, not_25_out);
  and and_6 (and_6_out, not_26_out, not_27_out, not_28_out, not_29_out, not_30_out);
  and and_7 (ExtOp_1, not_31_out, not_32_out, not_33_out);
  and and_8 (and_8_out, not_34_out, not_35_out, not_36_out, not_37_out, not_38_out, not_39_out);
  and and_9 (and_9_out, not_40_out, not_41_out, sw, beq, not_42_out);
  and and_10 (and_10_out, not_43_out, not_44_out, lw, beq, not_45_out);
  and and_11 (and_11_out, not_46_out, not_47_out, lw, sw, not_48_out);
  and and_12 (and_12_out, not_49_out, not_50_out, ori, not_51_out);
  and and_13 (and_13_out, not_52_out, not_53_out, not_54_out, not_55_out, not_56_out, lui);
  and and_14 (and_14_out, not_57_out, not_58_out, not_59_out, not_60_out, not_61_out, lui);
  or or_1 (RegWrite, and_3_out, and_4_out, and_5_out, and_6_out);
  or or_2 (ExtOp_0, and_8_out, and_9_out, and_10_out, and_11_out, and_12_out);
  or or_3 (ALUctr_1, and_13_out, ori);
  or or_4 (ALUctr_0, and_14_out, sub);

  assign MemtoReg = lw;
  assign MemWrite = sw;
  assign nPC_sel = beq;
endmodule

module EXT (
  input  [1:0] in_1,
  input  [15:0] in_2,
  output [31:0] out_3
);

  wire [31:0] bit_extender_1_out, bit_extender_2_out, bit_extender_3_out;

  assign bit_extender_1_out = {{16{1'b0}}, in_2};  // Bit_Extender bit_extender_1
  assign bit_extender_2_out = {{16{in_2[15]}}, in_2};  // Bit_Extender bit_extender_2
  assign bit_extender_3_out = {{16{1'b1}}, in_2};  // Bit_Extender bit_extender_3
  Multiplexer #(.select(2), .width(32), .enable("false")) multiplexer_1 (
    .in1(bit_extender_1_out), .in2(bit_extender_2_out), .in3(bit_extender_3_out), .out(out_3), .sel(in_1));  // open: in0
endmodule

module bCheck (
  input  branch,
  input  [5:0] bOp,
  input  [31:0] Grs,
  input  [31:0] Grt,
  output check
);

  wire and_1_out, and_2_out, and_3_out, and_4_out, and_5_out, and_6_out, and_7_out, and_8_out,
       comparator_1_eq, comparator_2_eq, comparator_2_gt, comparator_3_gt, comparator_4_eq, comparator_4_lt,
       comparator_5_lt, comparator_6_gt, comparator_6_lt, comparator_7_eq, comparator_8_eq, or_1_out,
       or_2_out, or_3_out;

  Comparator #(.width(32)) comparator_1 (.a(Grs), .b(Grt), .eq(comparator_1_eq));  // open: gt, lt
  Comparator #(.width(32)) comparator_2 (
    .a(Grs), .b({32{1'b0}}), .gt(comparator_2_gt), .eq(comparator_2_eq));  // open: lt
  Comparator #(.width(32)) comparator_3 (.a(Grs), .b({32{1'b0}}), .gt(comparator_3_gt));  // open: eq, lt
  Comparator #(.width(32)) comparator_4 (
    .a(Grs), .b({32{1'b0}}), .eq(comparator_4_eq), .lt(comparator_4_lt));  // open: gt
  Comparator #(.width(32)) comparator_5 (.a(Grs), .b({32{1'b0}}), .lt(comparator_5_lt));  // open: gt, eq
  Comparator #(.width(32)) comparator_6 (.a(Grs), .b(Grt), .gt(comparator_6_gt), .lt(comparator_6_lt));  // open: eq
  or or_1 (or_1_out, comparator_6_gt, comparator_6_lt);
  or or_2 (or_2_out, comparator_2_gt, comparator_2_eq);
  or or_3 (or_3_out, comparator_4_eq, comparator_4_lt);
  and and_1 (and_1_out, or_2_out, comparator_7_eq);
  Comparator #(.width(32), .mode("unsigned")) comparator_7 (.a(Grt), .b(32'h1), .eq(comparator_7_eq));  // open: gt, lt
  Comparator #(.width(32), .mode("unsigned")) comparator_8 (
    .a(Grt), .b({32{1'b0}}), .eq(comparator_8_eq));  // open: gt, lt
  and and_2 (and_2_out, comparator_5_lt, comparator_8_eq);
  and and_3 (and_3_out, bOp[5], branch, comparator_1_eq);
  and and_4 (and_4_out, bOp[4], branch, and_1_out);
  and and_5 (and_5_out, bOp[3], branch, comparator_3_gt);
  and and_6 (and_6_out, bOp[2], branch, or_3_out);
  and and_7 (and_7_out, bOp[1], branch, and_2_out);
  and and_8 (and_8_out, bOp[0], branch, or_1_out);
  or or_4 (check, and_3_out, and_4_out, and_5_out, and_6_out, and_7_out, and_8_out);
endmodule
